# Fritzing sketch breadboard (saved by Fritzing 0.9.3b)
breadboards: 1

parts:
  Teensy_3_1 = Teensy 3.1
  LED1 = LED - 5mm [color="Red (633nm)" package="5 mm [THT]"]
  R1 = Resistor [tolerance=±5% resistance=330 package=THT]
  S1 = Momentary Switch [package=ksa_sealed_tac_switch]
  U2 = POT [package=alps_pot]

nets:
  N1: Teensy_3_1.GND, LED1.cathode, U2.A
  N2: Teensy_3_1.D8, R1.Pin_0
  N3: Teensy_3_1.A2/D16, S1.3
  N4: Teensy_3_1.A8/D22, U2.S
  N5: LED1.anode, R1.Pin_1
  N6: S1.1, U2.E
